# Fritzing sketch Roverduino (saved by Fritzing 0.9.3b)
breadboards: 1

parts:
  R1 = Resistor [tolerance=±5% resistance=1k package=THT]
  M1 = DC Motor
  M2 = DC Motor
  hc-sr1 = hc-sr04
  Part1 = Arduino Uno (Rev3) - ICSP
  S1 = H-Bridge with L298N
  VCC1 = 4 x AAA Battery Mount

nets:
  N1: R1.Pin_0, Part1.D10_PWM/SS
  N2: R1.Pin_1, hc-sr1.Echo
  N3: M1.pin_1, S1.M2-02
  N4: M1.pin_2, S1.M2-01
  N5: M2.pin_1, S1.M1-02
  N6: M2.pin_2, S1.M1-01
  5V: hc-sr1.VCC, Part1.5V, S1.5V
  N7: hc-sr1.Trig, Part1.D11_PWM/MOSI
  GND: hc-sr1.GND, Part1.GND, S1.GND, VCC1.-
  N8: Part1.D8, S1.IN2
  N9: Part1.D9_PWM, S1.IN1
  N10: Part1.D3_PWM, S1.IN4
  N11: Part1.D4, S1.IN3
  N12: S1.12V, VCC1.+

custom parts:
  H-Bridge with L298N: h-bridge
